// Logisim project 4_bit_ALU.circ as structural Verilog: 6 circuits, main circuit main
module main (
);

  _4_bit_ALU u_4_bit_alu_1 ();  // open: in_1, in_2, in_3, out_4, out_5, out_6, out_7, out_8
endmodule

module _4_bit_AND (
  input  [3:0] in_1,
  input  [3:0] in_2,
  output [3:0] out_3
);

  and and_1 (out_3[0], in_1[0], in_2[0]);
  and and_2 (out_3[1], in_1[1], in_2[1]);
  and and_3 (out_3[2], in_1[2], in_2[2]);
  and and_4 (out_3[3], in_1[3], in_2[3]);
endmodule

module _4_bit_OR (
  input  [3:0] in_1,
  input  [3:0] in_2,
  output [3:0] out_3
);

  or or_1 (out_3[0], in_1[0], in_2[0]);
  or or_2 (out_3[1], in_1[1], in_2[1]);
  or or_3 (out_3[2], in_1[2], in_2[2]);
  or or_4 (out_3[3], in_1[3], in_2[3]);
endmodule

module _4_bit_ADD_SUB (
  input  in_1,
  input  [3:0] in_2,
  input  [3:0] in_3,
  output [3:0] out_4,
  output out_5,
  output out_6
);

  wire and_1_out, and_2_out, full_adder_1_out_5, full_adder_2_out_5, full_adder_3_out_5, not_1_out,
       not_2_out, not_3_out, xor_1_out, xor_2_out, xor_3_out, xor_4_out;

  not not_1 (not_1_out, out_4[3]);
  and and_1 (and_1_out, in_3[3], in_2[3], not_1_out);
  not not_2 (not_2_out, in_3[3]);
  not not_3 (not_3_out, in_2[3]);
  xor xor_1 (xor_1_out, in_3[0], in_1);
  xor xor_2 (xor_2_out, in_3[1], in_1);
  xor xor_3 (xor_3_out, in_3[2], in_1);
  xor xor_4 (xor_4_out, in_3[3], in_1);
  and and_2 (and_2_out, not_3_out, not_2_out, out_4[3]);
  FULL_ADDER full_adder_1 (.in_2(in_2[0]), .in_3(xor_1_out), .out_4(out_4[0]), .in_1(in_1), .out_5(full_adder_1_out_5));
  FULL_ADDER full_adder_2 (
    .in_2(in_2[1]), .in_3(xor_2_out), .out_4(out_4[1]), .in_1(full_adder_1_out_5), .out_5(full_adder_2_out_5));
  FULL_ADDER full_adder_3 (
    .in_2(in_2[2]), .in_3(xor_3_out), .out_4(out_4[2]), .in_1(full_adder_2_out_5), .out_5(full_adder_3_out_5));
  FULL_ADDER full_adder_4 (
    .in_2(in_2[3]), .in_3(xor_4_out), .out_4(out_4[3]), .in_1(full_adder_3_out_5), .out_5(out_5));
  or or_1 (out_6, and_2_out, and_1_out);
endmodule

module FULL_ADDER (
  input  in_1,
  input  in_2,
  input  in_3,
  output out_4,
  output out_5
);

  wire and_1_out, and_2_out, xor_1_out;

  and and_1 (and_1_out, in_2, in_3);
  or or_1 (out_5, and_1_out, and_2_out);
  xor xor_1 (xor_1_out, in_2, in_3);
  and and_2 (and_2_out, xor_1_out, in_1);
  xor xor_2 (out_4, in_1, xor_1_out);
endmodule

module _4_bit_ALU (
  input  [1:0] in_1,
  input  [3:0] in_2,
  input  [3:0] in_3,
  output out_4,
  output out_5,
  output [3:0] out_6,
  output out_7,
  output out_8
);

  wire or_1_out;
  wire [3:0] multiplexer_1_out, n4_bit_add_sub_1_out_4, n4_bit_and_1_out_3, n4_bit_or_1_out_3;

  _4_bit_AND u_4_bit_and_1 (.in_1(in_2), .in_2(in_3), .out_3(n4_bit_and_1_out_3));
  _4_bit_OR u_4_bit_or_1 (.in_1(in_2), .in_2(in_3), .out_3(n4_bit_or_1_out_3));
  _4_bit_ADD_SUB u_4_bit_add_sub_1 (
    .in_2(in_2), .in_3(in_3), .out_4(n4_bit_add_sub_1_out_4), .out_5(out_8), .out_6(out_7), .in_1(in_1[0]));
  Multiplexer #(.width(4)) multiplexer_1 (
    .in0(n4_bit_and_1_out_3), .in1(n4_bit_or_1_out_3), .out(multiplexer_1_out), .sel(in_1[0]));  // open: en
  Multiplexer #(.width(4)) multiplexer_2 (
    .in0(multiplexer_1_out), .in1(n4_bit_add_sub_1_out_4), .out({out_5, out_6[2:0]}), .sel(in_1[1]));  // open: en
  or or_1 (or_1_out, out_5, out_6[2], out_6[1], out_6[0]);
  not not_1 (out_4, or_1_out);

  assign out_6[3] = out_5;
endmodule
